# Fritzing sketch IRsensor (saved by Fritzing 0.8.7b)
breadboards: 1

parts:
  Componente1 = Arduino Uno (Rev3)
  IR1 = TSOP312.., 314.. [package=THT]

nets:
  N1: Componente1.D5_PWM, IR1.GND
  N2: Componente1.5V, IR1.Vs
  N3: Componente1.GND, IR1.Data
